# Fritzing sketch CG_Balance_V1.4 (saved by Fritzing 0.9.3b)
circuit board: 5.1cm x 4.1cm
breadboards: 1

parts:
  Mini_5V = Arduino Pro Mini (5V)
  R1 = Resistor [tolerance=±5% resistance=10k package=THT]
  R2 = Resistor [tolerance=±5% resistance=4.7k package=THT]
  VCC = Battery block 9V
  J2 = female pin header, 4 pins [form="♀ (female)"]
  J3 = female pin header, 4 pins [form="♀ (female)"]
  J1 = female pin header, 4 pins [form="♀ (female)"]

nets:
  N1: Mini_5V.VCC, J2.pin1, J3.pin1, J1.pin3
  N2: Mini_5V.GND, R2.Pin_0, VCC.-, J2.pin4, J3.pin4, J1.pin4
  N3: Mini_5V.A4, J1.pin1
  N4: Mini_5V.A5, J1.pin2
  N5: Mini_5V.A7, R1.Pin_0, R2.Pin_1
  N6: Mini_5V.RAW, R1.Pin_1, VCC.+
  N7: Mini_5V.A3, J2.pin2
  N8: Mini_5V.A2, J2.pin3
  N9: Mini_5V.A1, J3.pin2
  N10: Mini_5V.A0, J3.pin3

notes:
  CG_Scale F3x - Aneg Custom - 2017 - V1.4
  SDA
  SCL
  5V
  GND
  DT
  SCK
  RAW
  A5
  A4
  A7
